// Logisim project 2207097.circ as structural Verilog: 34 circuits, main circuit main
module main (
  input  [17:0] a,
  input  [17:0] b,
  input  [1:0] cin,
  output [17:0] Result,
  output out_5,
  output out_6,
  output out_7,
  output out_8
);

  wire zero_check_1_out_2;
  wire [17:0] n18_bit_adder_sub_1_out_4, n18_bit_or_1_out_3, n18bit_and_1_out_3;

  _18bit_AND u_18bit_and_1 (.in_1(a), .in_2(b), .out_3(n18bit_and_1_out_3));
  _18_bit_OR u_18_bit_or_1 (.in_1(a), .in_2(b), .out_3(n18_bit_or_1_out_3));
  _18_bit_Adder_Sub u_18_bit_adder_sub_1 (
    .cin(cin[0]), .B(b), .A(a), .out_4(n18_bit_adder_sub_1_out_4), .carry(out_5), .overflow(out_6));  // open: out_7
  Multiplexer #(.select(2), .width(18), .enable("false")) multiplexer_1 (
    .in0(n18bit_and_1_out_3), .in1(n18_bit_or_1_out_3), .in2(n18_bit_adder_sub_1_out_4),
    .in3(n18_bit_adder_sub_1_out_4), .out(Result), .sel(cin));
  _17th_bit_extract u_17th_bit_extract_1 (.in_1(Result), .out_2(out_7));
  not not_1 (out_8, zero_check_1_out_2);
  Zero_check zero_check_1 (.in_1(Result), .out_2(zero_check_1_out_2));

  // Notes on the sheet:
  //   Mutiur Rahman
  //   A
  //   B
  //   2207097
  //   00->AND
  //   01->OR
  //   10->ADD
  //   11->SUB
  //   zero
  //   result
  //   carry
  //   overflow
  //   negative 
endmodule

// AND
module _18bit_AND (
  input  [17:0] in_1,
  input  [17:0] in_2,
  output [17:0] out_3
);

  assign out_3 = in_1 & in_2;  // AND_Gate and_1, 18 bits wide

  // Notes on the sheet:
  //   2207097
endmodule

// OR
module _18_bit_OR (
  input  [17:0] in_1,
  input  [17:0] in_2,
  output [17:0] out_3
);

  assign out_3 = in_1 | in_2;  // OR_Gate or_1, 18 bits wide

  // Notes on the sheet:
  //   2207097
endmodule

module carry_generator (
  input  in_1,
  input  in_2,
  output G
);

  and and_1 (G, in_1, in_2);

  // Notes on the sheet:
  //   2207097
endmodule

// p
module carry_propagator (
  input  in_1,
  input  in_2,
  output p
);

  xor xor_1 (p, in_1, in_2);

  // Notes on the sheet:
  //   2207097
endmodule

module _4_bit_CLG (
  input  Cin,
  input  [3:0] A,
  input  [3:0] in_3,
  output c1,
  output c2,
  output c3,
  output c4
);

  wire and_1_out, and_2_out, and_3_out, and_4_out, and_5_out, and_6_out, and_7_out, and_8_out, and_9_out,
       and_10_out, carry_generator_1_g, carry_propagator_1_p, carry_propagator_2_p, carry_propagator_3_p,
       carry_propagator_4_p, G_2_g, G_3_g, G_g, or_2_out, xor_1_out, xor_2_out, xor_3_out, xor_4_out;

  xor xor_1 (xor_1_out, in_3[0], Cin);
  xor xor_2 (xor_2_out, in_3[1], Cin);
  xor xor_3 (xor_3_out, in_3[2], Cin);
  xor xor_4 (xor_4_out, in_3[3], Cin);
  and and_1 (and_1_out, Cin, carry_propagator_1_p);
  carry_generator carry_generator_1 (.in_1(A[0]), .in_2(xor_1_out), .G(carry_generator_1_g));
  carry_generator G (.in_1(A[1]), .in_2(xor_2_out), .G(G_g));
  carry_generator G_2 (.in_1(A[2]), .in_2(xor_3_out), .G(G_2_g));
  carry_generator G_3 (.in_1(A[3]), .in_2(xor_4_out), .G(G_3_g));
  carry_propagator carry_propagator_1 (.in_1(A[0]), .in_2(xor_1_out), .p(carry_propagator_1_p));
  carry_propagator carry_propagator_2 (.in_1(A[1]), .in_2(xor_2_out), .p(carry_propagator_2_p));
  carry_propagator carry_propagator_3 (.in_1(A[2]), .in_2(xor_3_out), .p(carry_propagator_3_p));
  carry_propagator carry_propagator_4 (.in_1(A[3]), .in_2(xor_4_out), .p(carry_propagator_4_p));
  or or_1 (c1, and_1_out, carry_generator_1_g);
  and and_2 (and_2_out, and_1_out, carry_propagator_2_p);
  and and_3 (and_3_out, carry_propagator_2_p, carry_generator_1_g);
  or or_2 (or_2_out, and_2_out, and_3_out);
  or or_3 (c2, or_2_out, G_g);
  and and_4 (and_4_out, carry_propagator_3_p, G_g);
  and and_5 (and_5_out, and_3_out, carry_propagator_3_p);
  and and_6 (and_6_out, and_2_out, carry_propagator_3_p);
  and and_7 (and_7_out, G_2_g, carry_propagator_4_p);
  and and_8 (and_8_out, and_4_out, carry_propagator_4_p);
  and and_9 (and_9_out, and_5_out, carry_propagator_4_p);
  and and_10 (and_10_out, and_6_out, carry_propagator_4_p);
  or or_4 (c3, and_4_out, and_5_out, and_6_out, G_2_g);
  or or_5 (c4, and_7_out, and_8_out, and_9_out, and_10_out, G_3_g);

  // Notes on the sheet:
  //   2207097
  //   B
  //   p2
  //   p3
  //   g0
  //   g1
  //   g2
  //   g3
  //   p0
  //   p1
endmodule

module _2_bit_CLG (
  input  Cin,
  input  [1:0] A,
  input  [1:0] in_3,
  output c1,
  output c2
);

  wire and_1_out, and_2_out, and_3_out, carry_propagator_1_p, carry_propagator_2_p, G_2_g, G_g, xor_1_out,
       xor_2_out;

  carry_propagator carry_propagator_1 (.in_1(A[0]), .in_2(xor_1_out), .p(carry_propagator_1_p));
  carry_propagator carry_propagator_2 (.in_1(A[1]), .in_2(xor_2_out), .p(carry_propagator_2_p));
  xor xor_1 (xor_1_out, in_3[0], Cin);
  xor xor_2 (xor_2_out, in_3[1], Cin);
  and and_1 (and_1_out, Cin, carry_propagator_1_p);
  carry_generator G (.in_1(A[0]), .in_2(xor_1_out), .G(G_g));
  carry_generator G_2 (.in_1(A[1]), .in_2(xor_2_out), .G(G_2_g));
  or or_1 (c1, and_1_out, G_g);
  and and_2 (and_2_out, G_g, carry_propagator_2_p);
  and and_3 (and_3_out, and_1_out, carry_propagator_2_p);
  or or_2 (c2, and_2_out, and_3_out, G_2_g);

  // Notes on the sheet:
  //   2207097
  //   B
  //   p1
  //   p0
  //   g0
  //   g1
endmodule

module Zero_check (
  input  [17:0] in_1,
  output out_2
);

  wire or_1_out;

  not not_1 (out_2, or_1_out);
  or or_1 (or_1_out, in_1[0], in_1[1], in_1[2], in_1[3], in_1[4], in_1[5], in_1[6], in_1[7], in_1[8], in_1[9], in_1[10], in_1[11], in_1[12], in_1[13], in_1[14], in_1[15], in_1[16], in_1[17]);

  // Notes on the sheet:
  //   2207097
  //   in
  //   out
endmodule

// CLG
module _18_bit_CLG (
  input  in_1,
  input  [17:0] in_2,
  input  [17:0] in_3,
  output [17:0] out_4
);

  _4_bit_CLG u_4_bit_clg_1 (
    .Cin(in_1), .A(in_2[3:0]), .in_3(in_3[3:0]), .c1(out_4[0]), .c2(out_4[1]), .c3(out_4[2]), .c4(out_4[3]));
  _4_bit_CLG u_4_bit_clg_2 (
    .Cin(out_4[3]), .A(in_2[7:4]), .in_3(in_3[7:4]), .c1(out_4[4]), .c2(out_4[5]), .c3(out_4[6]),
    .c4(out_4[7]));
  _4_bit_CLG u_4_bit_clg_3 (
    .Cin(out_4[7]), .A(in_2[11:8]), .in_3(in_3[11:8]), .c1(out_4[8]), .c2(out_4[9]), .c3(out_4[10]),
    .c4(out_4[11]));
  _4_bit_CLG u_4_bit_clg_4 (
    .Cin(out_4[11]), .A(in_2[15:12]), .in_3(in_3[15:12]), .c1(out_4[12]), .c2(out_4[13]), .c3(out_4[14]),
    .c4(out_4[15]));
  _2_bit_CLG u_2_bit_clg_1 (.Cin(out_4[15]), .A(in_2[17:16]), .in_3(in_3[17:16]), .c1(out_4[16]), .c2(out_4[17]));

  // Notes on the sheet:
  //   2207097
  //   cin
  //   A
  //   B
  //   cout
endmodule

// adder
module _1_bit_Adder (
  input  in_1,
  input  A,
  input  B,
  output sum,
  output Cout
);

  wire and_1_out, and_2_out, xor_1_out;

  xor xor_1 (xor_1_out, A, B);
  and and_1 (and_1_out, A, B);
  xor xor_2 (sum, in_1, xor_1_out);
  and and_2 (and_2_out, in_1, xor_1_out);
  or or_1 (Cout, and_2_out, and_1_out);

  // Notes on the sheet:
  //   2207097
  //   cin
endmodule

module _18_bit_Adder_Sub (
  input  cin,
  input  [17:0] A,
  input  [17:0] B,
  output [17:0] out_4,
  output carry,
  output overflow,
  output [17:0] out_7
);

  wire and_1_out, and_2_out, not_1_out, not_2_out, not_3_out;
  wire [17:0] bit_extender_1_out, xor_1_out;

  assign bit_extender_1_out = {{17{cin}}, cin};  // Bit_Extender bit_extender_1
  assign xor_1_out = bit_extender_1_out ^ B;  // XOR_Gate xor_1, 18 bits wide
  _18_bit_CLG u_18_bit_clg_1 (.in_1(cin), .in_2(A), .in_3(B), .out_4(out_7));
  _1_bit_Adder u_1_bit_adder_1 (.in_1(cin), .A(A[0]), .B(xor_1_out[0]), .sum(out_4[0]));  // open: Cout
  _1_bit_Adder u_1_bit_adder_2 (.in_1(out_7[0]), .A(A[1]), .B(xor_1_out[1]), .sum(out_4[1]));  // open: Cout
  _1_bit_Adder u_1_bit_adder_3 (.in_1(out_7[1]), .A(A[2]), .B(xor_1_out[2]), .sum(out_4[2]));  // open: Cout
  _1_bit_Adder u_1_bit_adder_4 (.in_1(out_7[2]), .A(A[3]), .B(xor_1_out[3]), .sum(out_4[3]));  // open: Cout
  _1_bit_Adder u_1_bit_adder_5 (.in_1(out_7[3]), .A(A[4]), .B(xor_1_out[4]), .sum(out_4[4]));  // open: Cout
  _1_bit_Adder u_1_bit_adder_6 (.in_1(out_7[4]), .A(A[5]), .B(xor_1_out[5]), .sum(out_4[5]));  // open: Cout
  _1_bit_Adder u_1_bit_adder_7 (.in_1(out_7[5]), .A(A[6]), .B(xor_1_out[6]), .sum(out_4[6]));  // open: Cout
  _1_bit_Adder u_1_bit_adder_8 (.in_1(out_7[6]), .A(A[7]), .B(xor_1_out[7]), .sum(out_4[7]));  // open: Cout
  _1_bit_Adder u_1_bit_adder_9 (.in_1(out_7[7]), .A(A[8]), .B(xor_1_out[8]), .sum(out_4[8]));  // open: Cout
  _1_bit_Adder u_1_bit_adder_10 (.in_1(out_7[8]), .A(A[9]), .B(xor_1_out[9]), .sum(out_4[9]));  // open: Cout
  _1_bit_Adder u_1_bit_adder_11 (.in_1(out_7[9]), .A(A[10]), .B(xor_1_out[10]), .sum(out_4[10]));  // open: Cout
  _1_bit_Adder u_1_bit_adder_12 (.in_1(out_7[10]), .A(A[11]), .B(xor_1_out[11]), .sum(out_4[11]));  // open: Cout
  _1_bit_Adder u_1_bit_adder_13 (.in_1(out_7[11]), .A(A[12]), .B(xor_1_out[12]), .sum(out_4[12]));  // open: Cout
  _1_bit_Adder u_1_bit_adder_14 (.in_1(out_7[12]), .A(A[13]), .B(xor_1_out[13]), .sum(out_4[13]));  // open: Cout
  _1_bit_Adder u_1_bit_adder_15 (.in_1(out_7[13]), .A(A[14]), .B(xor_1_out[14]), .sum(out_4[14]));  // open: Cout
  _1_bit_Adder u_1_bit_adder_16 (.in_1(out_7[14]), .A(A[15]), .B(xor_1_out[15]), .sum(out_4[15]));  // open: Cout
  _1_bit_Adder u_1_bit_adder_17 (.in_1(out_7[15]), .A(A[16]), .B(xor_1_out[16]), .sum(out_4[16]));  // open: Cout
  _1_bit_Adder u_1_bit_adder_18 (.in_1(out_7[16]), .A(A[17]), .B(xor_1_out[17]), .sum(out_4[17]), .Cout(carry));
  not not_1 (not_1_out, out_4[17]);
  not not_2 (not_2_out, A[17]);
  not not_3 (not_3_out, xor_1_out[17]);
  and and_1 (and_1_out, not_1_out, A[17], xor_1_out[17]);
  and and_2 (and_2_out, out_4[17], not_2_out, not_3_out);
  or or_1 (overflow, and_1_out, and_2_out);

  // Other names for the same wires on the sheet: _1 = out_7[0]; _2 = out_7[1]; _3 = out_7[2]; _4 = out_7[3];
  //   _5 = out_7[4]; _6 = out_7[5]; _7 = out_7[6]; _8 = out_7[7]; _9 = out_7[8]; _10 = out_7[9]; _11 = out_7[10];
  //   _12 = out_7[11]; _13 = out_7[12]; _14 = out_7[13]; _15 = out_7[14]; _16 = out_7[15]; _17 = out_7[16];
  //   _18 = out_7[17]

  // Notes on the sheet:
  //   2207097
  //   cin
  //   B
  //   sum
endmodule

module _17th_bit_extract (
  input  [17:0] in_1,
  output out_2
);


  assign out_2 = in_1[17];

  // Notes on the sheet:
  //   2207097
endmodule

module Booth_s_Multiplier (
  input  [17:0] M_input,
  input  [17:0] Q_input,
  input  Reset,
  output [17:0] out_4,
  output [17:0] out_5
);

  wire CLK_out, decoder_1_cl__a__q_1, decoder_1_dec_cnt, decoder_1_load__m__q__cnt, decoder_1_load_a,
       decoder_1_shr, or_1_out, Q_1_q0, Q_out, shift_register_1_out;
  wire [1:0] decoder_1_c0;
  wire [4:0] counter_1_q;
  wire [17:0] M_q17, main_1_result, n2_s_complement_1_out_2, n2_s_complement_2_out_2;

  Clock CLK (.out(CLK_out));
  // Probe on M_input
  Decoder decoder_1 (
    .Clk(CLK_out), .Reset(Reset), .Q0(out_4[0]), .Q_1(Q_1_q0), .Count(counter_1_q),
    .Cl__A__Q_1(decoder_1_cl__a__q_1), .LOad__M__Q__Cnt(decoder_1_load__m__q__cnt),
    .Load_A(decoder_1_load_a), .C0(decoder_1_c0[0]), .C1(decoder_1_c0[1]), .Shr(decoder_1_shr),
    .Dec_Cnt(decoder_1_dec_cnt));
  _2_s_complement u_2_s_complement_1 (.in_1(M_input), .out_2(n2_s_complement_1_out_2));
  or or_1 (or_1_out, decoder_1_load__m__q__cnt, decoder_1_dec_cnt);
  Counter #(.width(5), .max('h12)) counter_1 (
    .load(or_1_out), .D(5'b10010), .count(decoder_1_dec_cnt), .Q(counter_1_q), .clk(CLK_out));  // open: carry, clr
  _2_s_complement u_2_s_complement_2 (.in_1(Q_input), .out_2(n2_s_complement_2_out_2));
  // Probe on Q_input
  Shift_Register #(.length(18)) shift_register_1 (
    .shift(decoder_1_shr), .in(out_5[17]), .clk(CLK_out), .out(shift_register_1_out),
    .load(decoder_1_load_a), .clr(decoder_1_cl__a__q_1), .d0(main_1_result[17]), .q0(out_5[17]),
    .d1(main_1_result[16]), .q1(out_5[16]), .d2(main_1_result[15]), .q2(out_5[15]), .d3(main_1_result[14]),
    .q3(out_5[14]), .d4(main_1_result[13]), .q4(out_5[13]), .d5(main_1_result[12]), .q5(out_5[12]),
    .d6(main_1_result[11]), .q6(out_5[11]), .d7(main_1_result[10]), .q7(out_5[10]), .d8(main_1_result[9]),
    .q8(out_5[9]), .d9(main_1_result[8]), .q9(out_5[8]), .d10(main_1_result[7]), .q10(out_5[7]),
    .d11(main_1_result[6]), .q11(out_5[6]), .d12(main_1_result[5]), .q12(out_5[5]), .d13(main_1_result[4]),
    .q13(out_5[4]), .d14(main_1_result[3]), .q14(out_5[3]), .d15(main_1_result[2]), .q15(out_5[2]),
    .d16(main_1_result[1]), .q16(out_5[1]), .d17(main_1_result[0]), .q17(out_5[0]));
  Shift_Register #(.length(18)) M (
    .shift(1'b0), .clk(CLK_out), .load(decoder_1_load__m__q__cnt), .d0(n2_s_complement_1_out_2[17]),
    .q0(M_q17[17]), .d1(n2_s_complement_1_out_2[16]), .q1(M_q17[16]), .d2(n2_s_complement_1_out_2[15]),
    .q2(M_q17[15]), .d3(n2_s_complement_1_out_2[14]), .q3(M_q17[14]), .d4(n2_s_complement_1_out_2[13]),
    .q4(M_q17[13]), .d5(n2_s_complement_1_out_2[12]), .q5(M_q17[12]), .d6(n2_s_complement_1_out_2[11]),
    .q6(M_q17[11]), .d7(n2_s_complement_1_out_2[10]), .q7(M_q17[10]), .d8(n2_s_complement_1_out_2[9]),
    .q8(M_q17[9]), .d9(n2_s_complement_1_out_2[8]), .q9(M_q17[8]), .d10(n2_s_complement_1_out_2[7]),
    .q10(M_q17[7]), .d11(n2_s_complement_1_out_2[6]), .q11(M_q17[6]), .d12(n2_s_complement_1_out_2[5]),
    .q12(M_q17[5]), .d13(n2_s_complement_1_out_2[4]), .q13(M_q17[4]), .d14(n2_s_complement_1_out_2[3]),
    .q14(M_q17[3]), .d15(n2_s_complement_1_out_2[2]), .q15(M_q17[2]), .d16(n2_s_complement_1_out_2[1]),
    .q16(M_q17[1]), .d17(n2_s_complement_1_out_2[0]), .q17(M_q17[0]));  // open: in, out, clr
  main main_1 (.a(out_5), .b(M_q17), .cin(decoder_1_c0), .Result(main_1_result));  // open: out_5, out_6, out_7, out_8
  Shift_Register #(.length(18)) Q (
    .shift(decoder_1_shr), .in(shift_register_1_out), .clk(CLK_out), .out(Q_out),
    .load(decoder_1_load__m__q__cnt), .d0(n2_s_complement_2_out_2[17]), .q0(out_4[17]),
    .d1(n2_s_complement_2_out_2[16]), .q1(out_4[16]), .d2(n2_s_complement_2_out_2[15]), .q2(out_4[15]),
    .d3(n2_s_complement_2_out_2[14]), .q3(out_4[14]), .d4(n2_s_complement_2_out_2[13]), .q4(out_4[13]),
    .d5(n2_s_complement_2_out_2[12]), .q5(out_4[12]), .d6(n2_s_complement_2_out_2[11]), .q6(out_4[11]),
    .d7(n2_s_complement_2_out_2[10]), .q7(out_4[10]), .d8(n2_s_complement_2_out_2[9]), .q8(out_4[9]),
    .d9(n2_s_complement_2_out_2[8]), .q9(out_4[8]), .d10(n2_s_complement_2_out_2[7]), .q10(out_4[7]),
    .d11(n2_s_complement_2_out_2[6]), .q11(out_4[6]), .d12(n2_s_complement_2_out_2[5]), .q12(out_4[5]),
    .d13(n2_s_complement_2_out_2[4]), .q13(out_4[4]), .d14(n2_s_complement_2_out_2[3]), .q14(out_4[3]),
    .d15(n2_s_complement_2_out_2[2]), .q15(out_4[2]), .d16(n2_s_complement_2_out_2[1]), .q16(out_4[1]),
    .d17(n2_s_complement_2_out_2[0]), .q17(out_4[0]));  // open: clr
  Shift_Register #(.length(1)) Q_1 (
    .shift(decoder_1_shr), .in(Q_out), .clk(CLK_out), .clr(decoder_1_cl__a__q_1), .q0(Q_1_q0));  // open: out, load, d0
  // Probe on out_4

  // Notes on the sheet:
  //   2207097
endmodule

module Controller (
  input  Clk,
  input  Reset,
  input  Q0,
  input  Q_1,
  input  [2:0] Count,
  output Cl__A__Q_1,
  output LOad__M__Q__Cnt,
  output Load_A,
  output C0,
  output C1,
  output Shr,
  output Dec_Cnt
);

  wire and_3_out, multiplexer_1_out, not_1_out, not_2_out, not_3_out, not_4_out, not_5_out, not_6_out,
       not_7_out, or_2_out, Q0_prime_Q_1_out, Q0Q_1_prime_out;
  wire [1:0] rom_1_data_2;
  wire [2:0] and_1_out, and_2_out, bit_extender_1_out, bit_extender_2_out, bit_extender_3_out, CAR_q,
       or_1_out, rom_1_data;

  assign bit_extender_1_out = {{2{Q0_prime_Q_1_out}}, Q0_prime_Q_1_out};  // Bit_Extender bit_extender_1
  and Q0_prime_Q_1 (Q0_prime_Q_1_out, not_2_out, Q_1);
  not not_1 (not_1_out, Q0_prime_Q_1_out);
  assign bit_extender_2_out = {{2{not_1_out}}, not_1_out};  // Bit_Extender bit_extender_2
  assign and_1_out = 3'b100 & bit_extender_3_out & bit_extender_1_out;  // AND_Gate and_1, 3 bits wide
  assign or_1_out = and_1_out | rom_1_data | and_2_out;  // OR_Gate or_1, 3 bits wide
  not not_2 (not_2_out, Q0);
  assign and_2_out = bit_extender_2_out & bit_extender_3_out & 3'b101;  // AND_Gate and_2, 3 bits wide
  assign bit_extender_3_out = {{2{and_3_out}}, and_3_out};  // Bit_Extender bit_extender_3
  and and_3 (and_3_out, not_3_out, CAR_q[1], not_4_out);
  not not_3 (not_3_out, CAR_q[2]);
  not not_4 (not_4_out, CAR_q[0]);
  Counter #(.width(3), .max('h7)) CAR (
    .load(not_5_out), .D(or_1_out), .count(multiplexer_1_out), .Q(CAR_q), .clk(Clk), .clr(Reset));  // open: carry
  not not_5 (not_5_out, multiplexer_1_out);
  Multiplexer #(.select(2), .enable("false")) multiplexer_1 (
    .in0(1'b0), .in1(1'b1), .in2(Q0Q_1_prime_out), .in3(not_7_out), .out(multiplexer_1_out),
    .sel(rom_1_data_2));
  ROM #(.addrWidth(3), .dataWidth(12)) rom_1 (
    .addr(CAR_q), .data({Cl__A__Q_1, LOad__M__Q__Cnt, Load_A, C0, C1, Shr, Dec_Cnt, rom_1_data, rom_1_data_2}));  // open: sel
  and Q0Q_1_prime (Q0Q_1_prime_out, not_6_out, Q0);
  not not_6 (not_6_out, Q_1);
  or or_2 (or_2_out, Count[0], Count[1], Count[2]);
  not not_7 (not_7_out, or_2_out);

  // Notes on the sheet:
  //   To choose only
  //   state 2 (010)
  //   Control Word Format: Clear (A, Q-1), Load (M, Q, Cnt), Load A, C0, C1, Shr, Dec Cnt, Address bits (3 bit), Selection bits (2 bit)
  //   contents of rom_1 (hex, n*v repeats v):
  //   1 c01 2 394 281 61 b 1c
endmodule

module Decoder (
  input  Clk,
  input  Reset,
  input  Q0,
  input  Q_1,
  input  [4:0] Count,
  output Cl__A__Q_1,
  output LOad__M__Q__Cnt,
  output Load_A,
  output C0,
  output C1,
  output Shr,
  output Dec_Cnt
);

  wire a_1_da, a_1_db, a_1_dc, nor_1_out, T0, T2, T4, T6, T7;
  wire [2:0] T;

  nor nor_1 (nor_1_out, Count[0], Count[1], Count[2], Count[3], Count[4]);
  Decoder_part #(.select(3), .enable("false")) decoder_1 (
    .out0(T0), .out1(Cl__A__Q_1), .out2(T2), .out3(C0), .out4(T4), .out5(Dec_Cnt), .out6(T6), .out7(T7),
    .sel(T));
  a a_1 (.Q({Q0, Q_1}), .T(T), .C(nor_1_out), .DA(a_1_da), .DB(a_1_db), .DC(a_1_dc));
  D_Flip_Flop d_ff_1 (.clk(Clk), .D(a_1_da), .Q(T[0]), .reset(Reset));  // open: Qn, preset, en
  D_Flip_Flop d_ff_2 (.clk(Clk), .D(a_1_db), .Q(T[1]), .reset(Reset));  // open: Qn, preset, en
  D_Flip_Flop d_ff_3 (.clk(Clk), .D(a_1_dc), .Q(T[2]), .reset(Reset));  // open: Qn, preset, en
  or or_1 (Load_A, C0, T4);
  or or_2 (C1, T4, C0);

  assign LOad__M__Q__Cnt = Cl__A__Q_1;
  assign Shr = Dec_Cnt;

  // Other names for the same wires on the sheet: T1 = Cl__A__Q_1; T3 = C0; T5 = Dec_Cnt
endmodule

module a (
  input  [1:0] Q,
  input  [2:0] T,
  input  C,
  output DA,
  output DB,
  output DC
);

  wire and_1_out, and_2_out, and_3_out, and_4_out, and_5_out, or_4_out, or_5_out, Q0, Q1, Q2, Q3, T0, T1, T2,
       T3, T4, T5, T6, T7;

  Decoder_part #(.select(2), .enable("false")) decoder_1 (.out0(Q0), .out1(Q1), .out2(Q2), .out3(Q3), .sel(Q));
  Decoder_part #(.select(3), .enable("false")) decoder_2 (
    .out0(T0), .out1(T1), .out2(T2), .out3(T3), .out4(T4), .out5(T5), .out6(T6), .out7(T7), .sel(T));
  or or_1 (DA, T0, and_5_out, T3, T4, and_1_out, T7);
  or or_2 (DB, T1, and_2_out, T5, T6, T6, T7);
  or or_3 (DC, T5, and_3_out, T3, T4, and_4_out, T7);
  and and_1 (and_1_out, T6, C);
  and and_2 (and_2_out, T2, Q2);
  and and_3 (and_3_out, T2, or_5_out);
  and and_4 (and_4_out, T6, C);
  and and_5 (and_5_out, T2, or_4_out);
  or or_4 (or_4_out, Q0, Q2, Q3);
  or or_5 (or_5_out, Q0, Q1, Q3);
endmodule

module _2_s_complement (
  input  [17:0] in_1,
  output [17:0] out_2
);

  wire [16:0] not_1_out;
  wire [17:0] adder_1_out;

  not not_1 (not_1_out[0], in_1[0]);
  not not_2 (not_1_out[1], in_1[1]);
  not not_3 (not_1_out[2], in_1[2]);
  not not_4 (not_1_out[3], in_1[3]);
  not not_5 (not_1_out[4], in_1[4]);
  not not_6 (not_1_out[5], in_1[5]);
  not not_7 (not_1_out[6], in_1[6]);
  not not_8 (not_1_out[7], in_1[7]);
  not not_9 (not_1_out[8], in_1[8]);
  not not_10 (not_1_out[9], in_1[9]);
  not not_11 (not_1_out[10], in_1[10]);
  not not_12 (not_1_out[11], in_1[11]);
  not not_13 (not_1_out[12], in_1[12]);
  not not_14 (not_1_out[13], in_1[13]);
  not not_15 (not_1_out[14], in_1[14]);
  not not_16 (not_1_out[15], in_1[15]);
  not not_17 (not_1_out[16], in_1[16]);
  Multiplexer #(.width(18), .enable("false")) multiplexer_1 (
    .in0(in_1), .in1(adder_1_out), .out(out_2), .sel(in_1[17]));
  Adder #(.width(18)) adder_1 (.a({in_1[17], not_1_out}), .b(18'h1), .out(adder_1_out));  // open: cin, cout

  // Notes on the sheet:
  //   2207097
endmodule

module Memory_Buffer_Reg (
  input  load,
  input  [17:0] in_2,
  input  in_3,
  output [17:0] out_4
);

  wire CLK_out;

  Clock CLK (.out(CLK_out));
  _4_Bit_PLR u_4_bit_plr_1 (.in_2(in_2[3:0]), .in_3(CLK_out), .in_4(in_3), .LOAD(load), .out_5(out_4[3:0]));
  _4_Bit_PLR u_4_bit_plr_2 (.in_2(in_2[7:4]), .in_3(CLK_out), .in_4(in_3), .LOAD(load), .out_5(out_4[7:4]));
  _4_Bit_PLR u_4_bit_plr_3 (.in_2(in_2[11:8]), .in_3(CLK_out), .in_4(in_3), .LOAD(load), .out_5(out_4[11:8]));
  _4_Bit_PLR u_4_bit_plr_4 (.in_2(in_2[15:12]), .in_3(CLK_out), .in_4(in_3), .LOAD(load), .out_5(out_4[15:12]));
  _2_Bit_PLR u_2_bit_plr_1 (.in_2(in_2[17:16]), .in_3(CLK_out), .in_4(in_3), .LOAD(load), .out_5(out_4[17:16]));

  // Notes on the sheet:
  //   2207097
endmodule

module _2_Bit_PLR (
  input  LOAD,
  input  [1:0] in_2,
  input  in_3,
  input  in_4,
  output [1:0] out_5
);

  wire and_1_out, and_2_out, and_3_out, and_4_out, not_1_out, not_2_out;

  not not_1 (not_1_out, in_2[0]);
  not not_2 (not_2_out, in_2[1]);
  and and_1 (and_1_out, in_2[0], LOAD);
  and and_2 (and_2_out, not_1_out, LOAD);
  and and_3 (and_3_out, in_2[1], LOAD);
  and and_4 (and_4_out, not_2_out, LOAD);
  J_K_Flip_Flop j_k_ff_1 (
    .J(and_1_out), .clk(in_3), .K(and_2_out), .Q(out_5[0]), .reset(in_4));  // open: Qn, preset, en
  J_K_Flip_Flop j_k_ff_2 (
    .J(and_3_out), .clk(in_3), .K(and_4_out), .Q(out_5[1]), .reset(in_4));  // open: Qn, preset, en

  // Notes on the sheet:
  //   clock
  //   clear
  //   2207097
endmodule

module _4_Bit_PLR (
  input  LOAD,
  input  [3:0] in_2,
  input  in_3,
  input  in_4,
  output [3:0] out_5
);

  wire and_1_out, and_2_out, and_3_out, and_4_out, and_5_out, and_6_out, and_7_out, and_8_out, not_1_out,
       not_2_out, not_3_out, not_4_out;

  not not_1 (not_1_out, in_2[0]);
  not not_2 (not_2_out, in_2[1]);
  not not_3 (not_3_out, in_2[2]);
  not not_4 (not_4_out, in_2[3]);
  and and_1 (and_1_out, in_2[0], LOAD);
  and and_2 (and_2_out, not_1_out, LOAD);
  and and_3 (and_3_out, in_2[1], LOAD);
  and and_4 (and_4_out, not_2_out, LOAD);
  and and_5 (and_5_out, in_2[2], LOAD);
  and and_6 (and_6_out, not_3_out, LOAD);
  and and_7 (and_7_out, in_2[3], LOAD);
  and and_8 (and_8_out, not_4_out, LOAD);
  J_K_Flip_Flop j_k_ff_1 (
    .J(and_1_out), .clk(in_3), .K(and_2_out), .Q(out_5[0]), .reset(in_4));  // open: Qn, preset, en
  J_K_Flip_Flop j_k_ff_2 (
    .J(and_3_out), .clk(in_3), .K(and_4_out), .Q(out_5[1]), .reset(in_4));  // open: Qn, preset, en
  J_K_Flip_Flop j_k_ff_3 (
    .J(and_5_out), .clk(in_3), .K(and_6_out), .Q(out_5[2]), .reset(in_4));  // open: Qn, preset, en
  J_K_Flip_Flop j_k_ff_4 (
    .J(and_7_out), .clk(in_3), .K(and_8_out), .Q(out_5[3]), .reset(in_4));  // open: Qn, preset, en

  // Notes on the sheet:
  //   clear
  //   clock
  //   2207097
endmodule

module _18_Bit_CPL (
  input  lOAD,
  input  Count,
  input  [17:0] in_3,
  input  CLK,
  input  CLR,
  output [17:0] out_6
);

  wire n4_bit_cpl_1_cout, n4_bit_cpl_2_cout, n4_bit_cpl_3_cout, n4_bit_cpl_4_cout;

  _4_Bit_CPL u_4_bit_cpl_1 (
    .Cin(Count), .count(Count), .in_3(lOAD), .in_4(in_3[3:0]), .in_5(CLK), .clear(CLR), .out_7(out_6[3:0]),
    .Cout(n4_bit_cpl_1_cout));
  _4_Bit_CPL u_4_bit_cpl_2 (
    .Cin(n4_bit_cpl_1_cout), .count(Count), .in_3(lOAD), .in_4(in_3[7:4]), .in_5(CLK), .clear(CLR),
    .out_7(out_6[7:4]), .Cout(n4_bit_cpl_2_cout));
  _4_Bit_CPL u_4_bit_cpl_3 (
    .Cin(n4_bit_cpl_2_cout), .count(Count), .in_3(lOAD), .in_4(in_3[11:8]), .in_5(CLK), .clear(CLR),
    .out_7(out_6[11:8]), .Cout(n4_bit_cpl_3_cout));
  _4_Bit_CPL u_4_bit_cpl_4 (
    .Cin(n4_bit_cpl_3_cout), .count(Count), .in_3(lOAD), .in_4(in_3[15:12]), .in_5(CLK), .clear(CLR),
    .out_7(out_6[15:12]), .Cout(n4_bit_cpl_4_cout));
  _2_Bit_CPL u_2_bit_cpl_1 (
    .Cin(n4_bit_cpl_4_cout), .count(Count), .LOAD(lOAD), .in_4(in_3[17:16]), .CLR(CLR), .CLK(CLK),
    .out_7(out_6[17:16]));
  // Probe on out_6

  // Notes on the sheet:
  //   2207097
endmodule

module _2_Bit_CPL (
  input  Cin,
  input  count,
  input  LOAD,
  input  [1:0] in_4,
  input  CLR,
  input  CLK,
  output [1:0] out_7
);

  wire and_1_out, and_2_out, and_3_out, and_4_out, and_5_out, and_6_out, and_7_out, not_1_out, not_2_out,
       not_3_out, or_1_out, or_2_out, or_3_out, or_4_out;

  and and_1 (and_1_out, count, not_1_out);
  not not_1 (not_1_out, LOAD);
  not not_2 (not_2_out, in_4[0]);
  not not_3 (not_3_out, in_4[1]);
  and and_2 (and_2_out, LOAD, in_4[0]);
  and and_3 (and_3_out, LOAD, not_2_out);
  and and_4 (and_4_out, LOAD, in_4[1]);
  and and_5 (and_5_out, LOAD, not_3_out);
  and and_6 (and_6_out, and_1_out, Cin);
  and and_7 (and_7_out, and_1_out, Cin, out_7[0]);
  or or_1 (or_1_out, and_2_out, and_6_out);
  or or_2 (or_2_out, and_6_out, and_3_out);
  or or_3 (or_3_out, and_4_out, and_7_out);
  or or_4 (or_4_out, and_7_out, and_5_out);
  J_K_Flip_Flop j_k_ff_1 (.J(or_1_out), .clk(CLK), .K(or_2_out), .Q(out_7[0]), .reset(CLR));  // open: Qn, preset, en
  J_K_Flip_Flop j_k_ff_2 (.J(or_3_out), .clk(CLK), .K(or_4_out), .Q(out_7[1]), .reset(CLR));  // open: Qn, preset, en

  // Notes on the sheet:
  //   2207097
endmodule

module _4_Bit_CPL (
  input  Cin,
  input  count,
  input  in_3,
  input  [3:0] in_4,
  input  in_5,
  input  clear,
  output [3:0] out_7,
  output Cout
);

  wire and_1_out, and_2_out, and_3_out, and_4_out, and_5_out, and_6_out, and_7_out, and_8_out, and_9_out,
       and_10_out, and_11_out, and_12_out, and_13_out, not_1_out, not_2_out, not_3_out, not_4_out, not_5_out,
       or_1_out, or_2_out, or_3_out, or_4_out, or_5_out, or_6_out, or_7_out, or_8_out;

  not not_1 (not_1_out, in_3);
  and and_1 (and_1_out, count, not_1_out);
  not not_2 (not_2_out, in_4[0]);
  not not_3 (not_3_out, in_4[1]);
  not not_4 (not_4_out, in_4[2]);
  not not_5 (not_5_out, in_4[3]);
  and and_2 (and_2_out, in_3, in_4[0]);
  and and_3 (and_3_out, in_3, not_2_out);
  and and_4 (and_4_out, in_3, in_4[1]);
  and and_5 (and_5_out, in_3, not_3_out);
  and and_6 (and_6_out, in_3, in_4[2]);
  and and_7 (and_7_out, in_3, not_4_out);
  and and_8 (and_8_out, in_3, in_4[3]);
  and and_9 (and_9_out, in_3, not_5_out);
  and and_10 (and_10_out, and_1_out, Cin, out_7[0]);
  and and_11 (and_11_out, and_1_out, out_7[0], Cin, out_7[1], out_7[2]);
  or or_1 (or_1_out, and_2_out, and_12_out);
  and and_12 (and_12_out, and_1_out, Cin);
  or or_2 (or_2_out, and_12_out, and_3_out);
  or or_3 (or_3_out, and_4_out, and_10_out);
  or or_4 (or_4_out, and_10_out, and_5_out);
  or or_5 (or_5_out, and_6_out, and_13_out);
  and and_13 (and_13_out, out_7[0], Cin, out_7[1], and_1_out);
  or or_6 (or_6_out, and_13_out, and_7_out);
  or or_7 (or_7_out, and_8_out, and_11_out);
  or or_8 (or_8_out, and_11_out, and_9_out);
  J_K_Flip_Flop j_k_ff_1 (.J(or_1_out), .clk(in_5), .K(or_2_out), .Q(out_7[0]), .reset(clear));  // open: Qn, preset, en
  J_K_Flip_Flop j_k_ff_2 (.J(or_3_out), .clk(in_5), .K(or_4_out), .Q(out_7[1]), .reset(clear));  // open: Qn, preset, en
  J_K_Flip_Flop j_k_ff_3 (.J(or_5_out), .clk(in_5), .K(or_6_out), .Q(out_7[2]), .reset(clear));  // open: Qn, preset, en
  J_K_Flip_Flop j_k_ff_4 (.J(or_7_out), .clk(in_5), .K(or_8_out), .Q(out_7[3]), .reset(clear));  // open: Qn, preset, en
  and and_14 (Cout, out_7[2], out_7[0], out_7[1], out_7[3], and_1_out, Cin);
  // Probe on out_7

  // Notes on the sheet:
  //   load
  //   clock
  //   2207097
endmodule

module IR (
  input  LOAD,
  input  [3:0] in_2,
  input  in_3,
  output [3:0] out_4
);

  wire and_1_out, and_2_out, and_3_out, and_4_out, and_5_out, and_6_out, and_7_out, and_8_out, clock_1_out,
       not_1_out, not_2_out, not_3_out, not_4_out;

  not not_1 (not_1_out, in_2[0]);
  not not_2 (not_2_out, in_2[1]);
  not not_3 (not_3_out, in_2[2]);
  not not_4 (not_4_out, in_2[3]);
  Clock clock_1 (.out(clock_1_out));
  and and_1 (and_1_out, in_2[0], LOAD);
  and and_2 (and_2_out, not_1_out, LOAD);
  and and_3 (and_3_out, in_2[1], LOAD);
  and and_4 (and_4_out, not_2_out, LOAD);
  and and_5 (and_5_out, in_2[2], LOAD);
  and and_6 (and_6_out, not_3_out, LOAD);
  and and_7 (and_7_out, in_2[3], LOAD);
  and and_8 (and_8_out, not_4_out, LOAD);
  J_K_Flip_Flop j_k_ff_1 (
    .J(and_1_out), .clk(clock_1_out), .K(and_2_out), .Q(out_4[0]), .reset(in_3));  // open: Qn, preset, en
  J_K_Flip_Flop j_k_ff_2 (
    .J(and_3_out), .clk(clock_1_out), .K(and_4_out), .Q(out_4[1]), .reset(in_3));  // open: Qn, preset, en
  J_K_Flip_Flop j_k_ff_3 (
    .J(and_5_out), .clk(clock_1_out), .K(and_6_out), .Q(out_4[2]), .reset(in_3));  // open: Qn, preset, en
  J_K_Flip_Flop j_k_ff_4 (
    .J(and_7_out), .clk(clock_1_out), .K(and_8_out), .Q(out_4[3]), .reset(in_3));  // open: Qn, preset, en

  // Notes on the sheet:
  //   2207097
  //   Instruction Register
endmodule

module MAR (
  input  Load,
  input  [4:0] \input ,
  input  clk,
  input  Clear,
  output [4:0] out_5
);

  _4_Bit_PLR _4_Bit_PLR (.in_2(\input [3:0]), .in_3(clk), .in_4(Clear), .LOAD(Load), .out_5(out_5[3:0]));
  _1_Bit_PLR _1_Bit_PLR (.in_2(\input [4]), .in_3(clk), .in_4(Clear), .LOAD(Load), .out_5(out_5[4]));

  // Notes on the sheet:
  //   2207097
  //   Memory Address Register
endmodule

module PC (
  input  LOAD,
  input  count,
  input  [4:0] \input ,
  input  clk,
  input  CLEAR,
  output [4:0] out_6
);

  wire _4_Bit_CPL_cout;

  _4_Bit_CPL _4_Bit_CPL (
    .Cin(count), .count(count), .in_3(LOAD), .in_4(\input [3:0]), .in_5(clk), .clear(CLEAR),
    .out_7(out_6[3:0]), .Cout(_4_Bit_CPL_cout));
  _1_Bit_CPL _1_Bit_CPL (
    .Cin(_4_Bit_CPL_cout), .count(count), .LOAD(LOAD), .in_4(\input [4]), .CLR(CLEAR), .CLK(clk),
    .out_7(out_6[4]));
  // Probe on out_6

  // Notes on the sheet:
  //   2207097
  //   Program Counter
endmodule

module AR (
  input  load,
  input  [17:0] in_2,
  input  clk,
  input  clr,
  output [17:0] out_5
);

  _4_Bit_PLR _4_Bit_PLR (.in_2(in_2[3:0]), .in_3(clk), .in_4(clr), .LOAD(load), .out_5(out_5[3:0]));
  _4_Bit_PLR u_4_bit_plr_1 (.in_2(in_2[7:4]), .in_3(clk), .in_4(clr), .LOAD(load), .out_5(out_5[7:4]));
  _4_Bit_PLR u_4_bit_plr_2 (.in_2(in_2[11:8]), .in_3(clk), .in_4(clr), .LOAD(load), .out_5(out_5[11:8]));
  _4_Bit_PLR u_4_bit_plr_3 (.in_2(in_2[15:12]), .in_3(clk), .in_4(clr), .LOAD(load), .out_5(out_5[15:12]));
  _2_Bit_PLR _2_Bit_PLR (.in_2(in_2[17:16]), .in_3(clk), .in_4(clr), .LOAD(load), .out_5(out_5[17:16]));

  // Notes on the sheet:
  //   2207097
  //   Accumulator Register
endmodule

module _1_Bit_PLR (
  input  LOAD,
  input  in_2,
  input  in_3,
  input  in_4,
  output out_5
);

  wire and_1_out, and_2_out, not_1_out;

  not not_1 (not_1_out, in_2);
  and and_1 (and_1_out, in_2, LOAD);
  and and_2 (and_2_out, not_1_out, LOAD);
  J_K_Flip_Flop j_k_ff_1 (.J(and_1_out), .clk(in_3), .K(and_2_out), .Q(out_5), .reset(in_4));  // open: Qn, preset, en

  // Notes on the sheet:
  //   clock
  //   clear
  //   2207097
endmodule

module _1_Bit_CPL (
  input  Cin,
  input  count,
  input  LOAD,
  input  in_4,
  input  CLR,
  input  CLK,
  output out_7
);

  wire and_1_out, and_2_out, and_3_out, and_4_out, not_1_out, not_2_out, or_1_out, or_2_out;

  and and_1 (and_1_out, count, not_1_out);
  not not_1 (not_1_out, LOAD);
  not not_2 (not_2_out, in_4);
  and and_2 (and_2_out, LOAD, in_4);
  and and_3 (and_3_out, LOAD, not_2_out);
  and and_4 (and_4_out, and_1_out, Cin);
  or or_1 (or_1_out, and_2_out, and_4_out);
  or or_2 (or_2_out, and_4_out, and_3_out);
  J_K_Flip_Flop j_k_ff_1 (.J(or_1_out), .clk(CLK), .K(or_2_out), .Q(out_7), .reset(CLR));  // open: Qn, preset, en

  // Notes on the sheet:
  //   2207097
endmodule

module MBR (
  input  LOAD,
  input  COUNT,
  input  [17:0] in_3,
  input  in_4,
  input  clr,
  output [17:0] out_6
);

  _18_Bit_CPL _18_Bit_CPL (.Count(COUNT), .in_3(in_3), .CLK(in_4), .CLR(clr), .lOAD(LOAD), .out_6(out_6));

  // Notes on the sheet:
  //   2207097
  //   Memory Buffer Register
endmodule

module Control_Unit (
  input  reset,
  input  clock,
  input  flag_prime,
  input  [3:0] IR,
  input  zero_flag,
  output out_6,
  output out_7,
  output out_8,
  output out_9,
  output out_10,
  output out_11,
  output out_12,
  output out_13,
  output out_14,
  output out_15,
  output out_16,
  output out_17,
  output out_18,
  output out_19,
  output out_20,
  output out_21
);

  wire and_1_out, and_12_out, and_13_out, not_1_out, not_2_out, not_3_out, not_4_out, or_1_out, or_2_out,
       or_3_out, or_4_out, or_5_out, or_6_out, or_8_out, or_9_out, or_10_out, q0, q1, q2, q3, q4, q5, q6, q8,
       q9, q10, read__PC_plus_plus, t0, t1, t2, t3;
  wire [1:0] sgr_1_out_3;

  or or_1 (or_1_out, q10, q3);
  or or_2 (or_2_out, q10, q3);
  or or_3 (or_3_out, q10, q3);
  Decoder_part #(.select(4), .enable("false")) decoder_1 (
    .out0(q0), .out1(q1), .out2(q2), .out3(q3), .out4(q4), .out5(q5), .out6(q6), .out7(out_21), .out8(q8),
    .out9(q9), .out10(q10), .sel(IR));  // open: out11, out12, out13, out14, out15
  SGR sgr_1 (.in_1(clock), .in_2(reset), .out_3(sgr_1_out_3));
  not not_1 (not_1_out, flag_prime);
  or or_4 (or_4_out, q0, q1, or_1_out, q6, q8, q9);
  or or_5 (or_5_out, q2, q4, or_2_out);
  or or_6 (or_6_out, q0, q1, q2, or_3_out, q4, q6, q8, q9);
  and and_1 (and_1_out, flag_prime, or_4_out, t1);
  and and_2 (out_7, flag_prime, or_5_out, t3);
  not not_2 (not_2_out, flag_prime);
  and and_3 (out_20, flag_prime, t3);
  Decoder_part #(.select(2), .enable("false")) decoder_2 (
    .out0(t0), .out1(t1), .out2(t2), .out3(t3), .sel(sgr_1_out_3));
  // Probe on sgr_1_out_3
  and and_4 (read__PC_plus_plus, not_1_out, t1);
  and and_5 (out_19, not_2_out, or_6_out, t3);
  or or_7 (out_6, read__PC_plus_plus, and_1_out);
  or or_8 (or_8_out, q10, q3);
  or or_9 (or_9_out, q1, q8, q9);
  and and_6 (out_8, flag_prime, q0, t3);
  and and_7 (out_9, flag_prime, or_9_out, t3);
  and and_8 (out_10, flag_prime, q6, t3);
  and and_9 (out_11, flag_prime, q2, t2);
  and and_10 (out_12, flag_prime, or_8_out, t2);
  and and_11 (out_13, flag_prime, q4, t2);
  and and_12 (and_12_out, zero_flag, q3);
  or or_10 (or_10_out, and_12_out, q4);
  and and_13 (and_13_out, flag_prime, or_10_out, t3);
  not not_3 (not_3_out, flag_prime);
  not not_4 (not_4_out, flag_prime);
  or or_11 (out_14, read__PC_plus_plus, and_13_out);
  and and_14 (out_15, q5, t3);
  and and_15 (out_16, not_3_out, t0);
  and and_16 (out_17, flag_prime, t0);
  and and_17 (out_18, not_4_out, t2);

  // Other names for the same wires on the sheet: a1__AND = out_8; a2__ADD = out_9; a3__LOAD = out_10;
  //   b1_B__A = out_11; b2_B__b = out_12; b3____b_op_0101_b_ad___pc = out_13; c1_pc_plus_plus = out_14;
  //   c2_pc_B_ad = out_15; clk = clock; d1_mar_pc = out_16; d2_mar_B_ad = out_17; F = flag_prime; f2 = out_20;
  //   f_0 = out_20; exe_start = out_19; f_1 = out_19; i1_IR_B_op = out_18; M_read_b__M = out_6; M_write_B__M = out_7;
  //   q7 = out_21; res = reset; zero = zero_flag

  // Notes on the sheet:
  //   READ
  //   Write
  //   Execution
  //   Fetch Start
  //   2207097
  //   INC IF Zero
  //   JMP
  //   PC INC
endmodule

module SGR (
  input  in_1,
  input  in_2,
  output [1:0] out_3
);

  J_K_Flip_Flop j_k_ff_1 (.J(1'b1), .clk(in_1), .K(1'b1), .Q(out_3[0]), .reset(in_2));  // open: Qn, preset, en
  J_K_Flip_Flop j_k_ff_2 (.J(out_3[0]), .clk(in_1), .K(out_3[0]), .Q(out_3[1]), .reset(in_2));  // open: Qn, preset, en
endmodule

module CPU (
  input  Reset
);

  wire a1, a2, a3, b1, b2, b3, Bz, c1, c2, clk, clock_1_out, d1, d2, f1, f2, i1, j_k_ff_1_q, LOAD_A, LOAD_B,
       LoadPc, or_2_out, R, s, S_qn, W;
  wire [1:0] alu_control_1_out_2;
  wire [3:0] IR;
  wire [4:0] MAR, multiplexer_1_out, multiplexer_2_out;
  wire [17:0] A, B, mdata, multiplexer_3_out, multiplexer_4_out, pcdata, Res;

  or or_1 (LoadPc, c2, b3);
  Clock clock_1 (.out(clock_1_out));
  or or_2 (or_2_out, d1, d2);
  Multiplexer #(.width(5), .enable("false")) multiplexer_1 (.in0(MAR), .in1(B[4:0]), .out(multiplexer_1_out), .sel(c2));
  PC PC (.count(c1), .\input (multiplexer_1_out), .clk(clk), .CLEAR(Reset), .LOAD(LoadPc), .out_6(pcdata[4:0]));
  Multiplexer #(.width(5), .enable("false")) multiplexer_2 (
    .in0(pcdata[4:0]), .in1(B[4:0]), .out(multiplexer_2_out), .sel(d2));
  MAR mar_1 (.\input (multiplexer_2_out), .clk(clk), .Clear(Reset), .Load(or_2_out), .out_5(MAR));
  J_K_Flip_Flop j_k_ff_1 (.J(f1), .clk(clock_1_out), .K(f2), .Q(j_k_ff_1_q), .reset(Reset));  // open: Qn, preset, en
  IR u_IR (.in_2(B[11:8]), .in_3(Reset), .LOAD(i1), .out_4(IR));
  D_Flip_Flop u_S (.clk(clock_1_out), .Qn(S_qn), .preset(s), .reset(Reset));  // open: D, Q, en
  Multiplexer #(.select(2), .width(18), .enable("false")) multiplexer_3 (
    .in0({pcdata[17:12], 4'b0101, pcdata[7:0]}), .in1(mdata), .in2(A), .out(multiplexer_3_out), .sel({b1, R}));  // open: in3
  Multiplexer #(.width(18), .enable("false")) multiplexer_4 (.in0(Res), .in1(B), .out(multiplexer_4_out), .sel(a3));
  // Probe on multiplexer_4_out
  and and_1 (clk, S_qn, clock_1_out);
  ALU_Control alu_control_1 (.IR(IR), .out_2(alu_control_1_out_2));
  AR ACR (.in_2(multiplexer_4_out), .clk(clk), .clr(Reset), .load(LOAD_A), .out_5(A));
  Control_Unit Control_Unit (
    .reset(Reset), .clock(clk), .flag_prime(j_k_ff_1_q), .IR(IR), .zero_flag(Bz), .out_6(R), .out_7(W),
    .out_8(a1), .out_9(a2), .out_10(a3), .out_11(b1), .out_12(b2), .out_13(b3), .out_14(c1), .out_15(c2),
    .out_16(d1), .out_17(d2), .out_18(i1), .out_19(f1), .out_20(f2), .out_21(s));
  MBR MBR (.LOAD(LOAD_B), .COUNT(b2), .in_3(multiplexer_3_out), .in_4(clk), .clr(Reset), .out_6(B));
  main ALU (.a(A), .b(B), .cin(alu_control_1_out_2), .Result(Res));  // open: out_5, out_6, out_7, out_8
  // Probe on A
  or or_3 (LOAD_A, a1, a2, a3);
  // Probe on LOAD_A
  Zero_check Zero_Check (.in_1(B), .out_2(Bz));
  RAM #(.addrWidth(5), .dataWidth(18), .bus("separate")) ram_1 (
    .addr(MAR), .din(B), .data(mdata), .str(W), .clk(clk), .ld(R));  // open: sel, clr
  or or_4 (LOAD_B, b1, R, b3);
  // Probe on B
  // Probe on Res

  // Other names for the same wires on the sheet: BAD[4:0] = B[4:0]; Bop[3:0] = B[11:8]; sbit[1:0] = {b1, R}

  // Notes on the sheet:
  //   2207097
endmodule

module ALU_Control (
  input  [3:0] IR,
  output [1:0] out_2
);

  Multiplexer #(.select(4), .width(2), .enable("false")) multiplexer_1 (
    .in0(2'b00), .in1(2'b10), .in2(2'b00), .in3(2'b00), .in4(2'b00), .in5(2'b00), .in6(2'b00), .in7(2'b00),
    .in8(2'b01), .in9(2'b11), .in10(2'b00), .in11(2'b00), .in12(2'b00), .in13(2'b00), .in14(2'b00),
    .in15(2'b00), .out(out_2), .sel(IR));
  // Probe on out_2

  // Notes on the sheet:
  //   2207097
endmodule
